# Fritzing sketch timetemp_sketch (saved by Fritzing 0.9.2b)
breadboards: 1

parts:
  Pi1 = Adafruit Pi Cobbler
  BMP1 = BMP085 Breakout
  BB1 = 4-Line Bi-Directional Level Shifter
  7SEG1 = 7-Segment LED I2C Backpack (yellow)
  7SEG2 = 7-Segment LED I2C Backpack (green)

nets:
  N1: Pi1.3V3, BMP1.3Vo
  N2: Pi1.5V0, BB1.HV, 7SEG1.V+, 7SEG2.V+
  N3: Pi1.SDA0, BMP1.SDA, BB1.A2
  N4: Pi1.SCL0, BMP1.SCL, BB1.A1
  N5: Pi1.PIN19, BB1.LV
  GND: Pi1.PIN20, Pi1.PIN25, BMP1.GND, BB1.GND, 7SEG1.GND, 7SEG2.GND
  N6: BB1.B1, 7SEG1.SCL, 7SEG2.SCL
  N7: BB1.B2, 7SEG1.SDA, 7SEG2.SDA

custom parts:
  Adafruit Pi Cobbler: Adafruit Pi Cobbler GPIO Breakout for Raspberry Pi
  BMP085 Breakout: A breakout for the BMP085 barometric pressure and temperature sensor
  4-Line Bi-Directional Level Shifter: 4-Channel Bi-Directional Level Shifter
  7-Segment LED I2C Backpack (yellow): 4-digit, 7-segment LED Display with I2C Control
  7-Segment LED I2C Backpack (green): 4-digit, 7-segment LED Display with I2C Control
